# Fritzing sketch Fritzing ESP8266 (saved by Fritzing 0.9.3b)
circuit board: 6.89651cm x 6.54362cm
breadboards: 1

parts:
  LEFT = Dagu DGServo 9g header (male) [package=THT]
  VCC1 = 4 x AAA Battery Mount
  U2 = NodeMCU V1.0
  RIGHT = Dagu DGServo 9g header (male) [package=THT]
  S1 = Square Pushbutton
  J1 = Basic Servo
  J2 = Basic Servo

nets:
  GND: LEFT.gnd, VCC1.-, U2.GND, RIGHT.gnd, S1.leg0, J1.gnd, J2.gnd
  5V: LEFT.Vcc, VCC1.+, U2.Vin, RIGHT.Vcc, J1.vcc, J2.vcc
  N1: LEFT.pulse, U2.D5, J1.pulse
  N2: U2.D0, S1.leg1
  N3: U2.D6, RIGHT.pulse, J2.pulse

custom parts:
  NodeMCU V1.0: ESP8266 based NodeMCU
